// Logisim project tt_test.circ as structural Verilog: 1 circuit, main circuit main
module main (
  input  RST,
  input  CLK,
  output O_1,
  output O_2,
  output O_3,
  output O_0
);

  wire d_ff_1_qn, d_ff_2_qn, d_ff_3_qn, d_ff_4_qn, nand_1_out, not_1_out, not_2_out, not_3_out, not_4_out,
       or_1_out, or_2_out, or_3_out;

  D_Flip_Flop d_ff_1 (.D(nand_1_out), .clk(CLK), .Q(O_0), .Qn(d_ff_1_qn));  // open: preset, reset
  not not_1 (not_1_out, or_1_out);
  or or_1 (or_1_out, RST, d_ff_1_qn);
  D_Flip_Flop d_ff_2 (.D(not_1_out), .clk(CLK), .Q(O_1), .Qn(d_ff_2_qn));  // open: preset, reset
  D_Flip_Flop d_ff_3 (.D(not_2_out), .clk(CLK), .Q(O_2), .Qn(d_ff_3_qn));  // open: preset, reset
  not not_2 (not_2_out, or_2_out);
  or or_2 (or_2_out, RST, d_ff_2_qn);
  or or_3 (or_3_out, RST, d_ff_3_qn);
  D_Flip_Flop d_ff_4 (.D(not_3_out), .clk(CLK), .Q(O_3), .Qn(d_ff_4_qn));  // open: preset, reset
  not not_3 (not_3_out, or_3_out);
  nand nand_1 (nand_1_out, d_ff_4_qn, not_4_out);
  not not_4 (not_4_out, RST);
endmodule
